# Fritzing sketch devre (saved by Fritzing 0.9.3b)
breadboards: 1

parts:
  T3_Vakfı1 = Generic shrouded header - 32 pins [package=THT]
  Parça1 = MQ-4
  Parça2 = FC-28 Soil Hygrometer Module
  Parça3 = FC-28 Soil Hygrometer Module - Probe
  S1 = KY-026
  ZS-042_RTC1 = ZS-042 RTC Module
  FC-1 = Sound Sensor
  J1 = Basic Servo
  J2 = Piezo Speaker
  Parça4 = RFID-RC522-v2
  LCD2004-I2C1 = LCD2004-I2C
  LCD2004-I2C2 = LCD2004-I2C

nets:
  N1: T3_Vakfı1.pin2, Parça2.AO
  N2: T3_Vakfı1.pin3, Parça1.AO
  N3: T3_Vakfı1.pin4, FC-1.OUT
  N4: T3_Vakfı1.pin13, J2.pin2
  VCC: T3_Vakfı1.pin15, Parça1.VCC, Parça2.VCC, S1.pin3, ZS-042_RTC1.VCC, FC-1.VCC, J1.vcc, Parça4.3.3V, LCD2004-I2C2.VCC
  GND: T3_Vakfı1.pin16, Parça1.GND, Parça2.GND, S1.pin2, ZS-042_RTC1.GND, FC-1.GND, J1.gnd, J2.pin1, Parça4.GND, LCD2004-I2C2.GND
  N5: T3_Vakfı1.pin20, ZS-042_RTC1.SDA, LCD2004-I2C2.SCL
  N6: T3_Vakfı1.pin21, ZS-042_RTC1.SCL, LCD2004-I2C1.SDA
  N7: T3_Vakfı1.pin23, Parça4.SDA
  N8: T3_Vakfı1.pin24, Parça4.MOSI
  N9: T3_Vakfı1.pin25, Parça4.MISO
  N10: T3_Vakfı1.pin26, Parça4.SCK
  N11: T3_Vakfı1.pin27, Parça4.RST
  N12: T3_Vakfı1.pin30, J1.pulse
  N13: T3_Vakfı1.pin31, S1.pin4
  N14: Parça2.POS, Parça3.POS
  N15: Parça2.NEG, Parça3.NEG

notes:
  Tüm + pinleri + hattına.
  Tüm - pinleri - hattına.
  Gaz Sinyal=A1
  Nem=A0
  Ateş=D0
  Ses=A2
  Servo=D1
  Buzzer=D12
  MISO=MISO
  MOSI=MOSI
  RST=D4
  SDA=D8
  SCK=SCK
  SCL=SCL
  SDA=SDA

custom parts:
  Generic shrouded header - 32 pins: Ülkemizin mühendislik kaynakları kullanılarak geliştirilen Deneyap Kart; güçlü işlemcisi, dayanıklı tasarımı ve çok yönlü giriş/çıkış pinleri ile kullanıcılara Elektronik Programlama, Nesnelerin İnterneti (IoT) ve Yapay Zeka alanlarında başlangıç seviyesinden endüstriyel uygulamalara kadar her seviyede projeyi yapma imkanı sunuyor.
  FC-28 Soil Hygrometer Module: The FC-28 is a soil hygrometer module that uses the Texas Instruments LM393 comparator chip to provide an analog measurement of soil humidity. The digital output is high when soil moisture is over a certain threshold, as determined by adjusting the potentiometer.
  FC-28 Soil Hygrometer Module - Probe: The FC-28 is a soil hygrometer module that uses the Texas Instruments LM393 comparator chip to provide an analog measurement of soil humidity.
  KY-026: ky-026 flame sensor module
  RFID-RC522-v2: A simple China made RFID-RC522 Reader; do check the pin labels, as this is a MFRC522 based clone.
  LCD2004-I2C: A standard character display with 4x20 characters. Comes in many colors with LCM2004 IIC attached.
